// Logisim project first_logsim.circ as structural Verilog: 5 circuits, main circuit main
module main (
  input  a,
  input  b,
  input  carry,
  output sum,
  output carry2
);

  wire nand_1_out, nand_2_out, nand_3_out, nand_4_out, nand_5_out, nand_6_out, nand_7_out, nand_8_out,
       nand_9_out, nand_10_out, nand_11_out, nand_12_out, nand_13_out;

  nand nand_1 (nand_1_out, a, a);
  nand nand_2 (nand_2_out, b, b);
  nand nand_3 (nand_3_out, a, a);
  nand nand_4 (nand_4_out, carry, carry);
  nand nand_5 (nand_5_out, b, b);
  nand nand_6 (nand_6_out, carry, carry);
  nand nand_7 (nand_7_out, b, carry);
  nand nand_8 (nand_8_out, a, carry);
  nand nand_9 (nand_9_out, a, b);
  nand nand_10 (nand_10_out, nand_1_out, nand_2_out, carry);
  nand nand_11 (nand_11_out, nand_3_out, b, nand_4_out);
  nand nand_12 (nand_12_out, a, nand_5_out, nand_6_out);
  nand nand_13 (nand_13_out, a, b, carry);
  nand nand_14 (carry2, nand_7_out, nand_8_out, nand_9_out);
  nand nand_15 (sum, nand_10_out, nand_11_out, nand_12_out, nand_13_out);
endmodule

// HA
module half_adder (
  input  A,
  input  B,
  output S,
  output C
);

  and and_1 (C, A, B);
  xor xor_1 (S, A, B);

  // Notes on the sheet:
  //   한글도 되나...
endmodule

// FA
module full_adder (
  input  A,
  input  B,
  input  Cin,
  output S,
  output Cout
);

  wire half_adder_1_c, half_adder_1_s, half_adder_2_c;

  half_adder half_adder_1 (.A(A), .B(B), .S(half_adder_1_s), .C(half_adder_1_c));
  half_adder half_adder_2 (.A(half_adder_1_s), .B(Cin), .S(S), .C(half_adder_2_c));
  or or_1 (Cout, half_adder_2_c, half_adder_1_c);
endmodule

module _1x2_Mux (
  input  in_0,
  input  in_1,
  input  select,
  output out
);

  wire and_1_out, and_2_out, not_1_out;

  not not_1 (not_1_out, select);
  and and_1 (and_1_out, in_0, not_1_out);
  and and_2 (and_2_out, in_1, select);
  or or_1 (out, and_1_out, and_2_out);
endmodule

module _2x4_Mux (
  input  in_00,
  input  in_01,
  input  in_10,
  input  in_11,
  input  sel_0,
  input  sel_1,
  output out
);

  wire n1x2_mux_1_out, n1x2_mux_2_out;

  _1x2_Mux u_1x2_mux_1 (.in_0(in_00), .in_1(in_01), .select(sel_1), .out(n1x2_mux_1_out));
  _1x2_Mux u_1x2_mux_2 (.in_0(in_10), .in_1(in_11), .select(sel_1), .out(n1x2_mux_2_out));
  _1x2_Mux u_1x2_mux_3 (.in_0(n1x2_mux_1_out), .in_1(n1x2_mux_2_out), .select(sel_0), .out(out));
endmodule
