// Logisim project hw1-adder.circ as structural Verilog: 8 circuits, main circuit main
module main (
  input  a,
  input  b,
  input  c,
  input  d,
  output x,
  output y
);

  wire and_1_out, and_2_out, nand_1_out, nand_2_out;

  nand nand_1 (nand_1_out, a, b);
  nand nand_2 (nand_2_out, c, d);
  and and_1 (and_1_out, a, b);
  and and_2 (and_2_out, c, d);
  nand nand_3 (x, nand_1_out, nand_2_out);
  or or_1 (y, and_1_out, and_2_out);
endmodule

module NAND (
  input  in_1,
  input  in_2,
  input  in_3,
  input  in_4,
  output out_5,
  output out_6
);

  wire and_1_out, not_1_out, not_2_out;

  not not_1 (not_1_out, in_3);
  not not_2 (not_2_out, in_4);
  and and_1 (and_1_out, in_1, in_2);
  not not_3 (out_5, and_1_out);
  or or_1 (out_6, not_1_out, not_2_out);
endmodule

module DeMorgan (
  input  a,
  input  b,
  input  c,
  input  d,
  output x,
  output y
);

  wire and_1_out, and_2_out, nand_1_out, nand_2_out;

  nand nand_1 (nand_1_out, a, b);
  nand nand_2 (nand_2_out, c, d);
  and and_1 (and_1_out, a, b);
  and and_2 (and_2_out, c, d);
  nand nand_3 (x, nand_1_out, nand_2_out);
  or or_1 (y, and_1_out, and_2_out);
endmodule

module RS_latch (
  input  R,
  input  S,
  input  nS,
  input  nR,
  output out_5,
  output out_6,
  output Q,
  output nQ
);

  nor nor_1 (out_5, R, out_6);
  nor nor_2 (out_6, out_5, S);
  nand nand_1 (Q, nS, nQ);
  nand nand_2 (nQ, Q, nR);
endmodule

// HA
module half_adder (
  input  A,
  input  B,
  output S,
  output C
);

  xor xor_1 (S, A, B);
  and and_1 (C, A, B);
endmodule

// FA
module full_adder (
  input  A,
  input  B,
  input  Cin,
  output S,
  output Cout
);

  wire half_adder_1_c, half_adder_2_c, half_adder_2_s;

  half_adder half_adder_1 (.A(half_adder_2_s), .B(Cin), .S(S), .C(half_adder_1_c));
  half_adder half_adder_2 (.A(A), .B(B), .S(half_adder_2_s), .C(half_adder_2_c));
  or or_1 (Cout, half_adder_1_c, half_adder_2_c);
endmodule

module _4bit_adder (
  input  Cin,
  input  A0,
  input  A1,
  input  A2,
  input  A3,
  input  B0,
  input  B1,
  input  B2,
  input  B3,
  output S0,
  output S1,
  output S2,
  output S3,
  output Cout
);

  wire full_adder_1_cout, full_adder_2_cout, full_adder_3_cout;

  full_adder full_adder_1 (.A(A0), .B(B0), .Cin(Cin), .S(S0), .Cout(full_adder_1_cout));
  full_adder full_adder_2 (.A(A1), .B(B1), .Cin(full_adder_1_cout), .S(S1), .Cout(full_adder_2_cout));
  full_adder full_adder_3 (.A(A2), .B(B2), .Cin(full_adder_2_cout), .S(S2), .Cout(full_adder_3_cout));
  full_adder full_adder_4 (.A(A3), .B(B3), .Cin(full_adder_3_cout), .S(S3), .Cout(Cout));
endmodule

module _4bit_adder_2 (
  input  Cin,
  input  [3:0] in_2,
  input  [3:0] in_3,
  output [3:0] out_4,
  output Cout
);

  wire full_adder_1_cout, full_adder_2_cout, full_adder_3_cout;

  full_adder full_adder_1 (.A(in_2[0]), .B(in_3[0]), .Cin(Cin), .S(out_4[0]), .Cout(full_adder_1_cout));
  full_adder full_adder_2 (.A(in_2[1]), .B(in_3[1]), .Cin(full_adder_1_cout), .S(out_4[1]), .Cout(full_adder_2_cout));
  full_adder full_adder_3 (.A(in_2[2]), .B(in_3[2]), .Cin(full_adder_2_cout), .S(out_4[2]), .Cout(full_adder_3_cout));
  full_adder full_adder_4 (.A(in_2[3]), .B(in_3[3]), .Cin(full_adder_3_cout), .S(out_4[3]), .Cout(Cout));
endmodule
