// Logisim project hw2-flipflop.circ as structural Verilog: 7 circuits, main circuit main
module main (
  input  in_1,
  input  [3:0] in_2,
  input  in_3,
  input  in_4,
  output [3:0] out_5,
  output [3:0] out_6,
  output [3:0] out_7
);

  wire clock_1_out;

  Clock clock_1 (.out(clock_1_out));
  // _4bit_register 4bit_register_1: pin names not known; wires that end beside it: in_2, clock_1_out, out_6, in_3, out_5
  // _4bit_register 4bit_register_2: pin names not known; wires that end beside it: out_6, clock_1_out, in_4, out_7
  _4bit_adder_2 u_4bit_adder_2_1 (.Cin(in_1), .A(out_5), .B(out_7), .S(out_6));  // open: Cout
endmodule

module SR_Latch (
  input  R,
  input  S,
  input  nS,
  input  nR,
  output Q,
  output nQ,
  output Q_2,
  output nQ_2
);

  nor nor_1 (Q, R, nQ);
  nor nor_2 (nQ, Q, S);
  nand nand_1 (Q_2, nS, nQ_2);
  nand nand_2 (nQ_2, Q_2, nR);
endmodule

module Gated_SR_Latch (
  input  R,
  input  E,
  input  S,
  output Q,
  output nQ
);

  wire and_1_out, and_2_out;

  and and_1 (and_1_out, R, E);
  and and_2 (and_2_out, E, S);
  nor nor_1 (Q, and_1_out, nQ);
  nor nor_2 (nQ, Q, and_2_out);
endmodule

// D latch
module Gated_D_Latch (
  input  clear,
  input  D,
  input  E,
  output Q,
  output nQ
);

  wire and_1_out, and_2_out, not_1_out;

  not not_1 (not_1_out, D);
  and and_1 (and_1_out, not_1_out, E);
  and and_2 (and_2_out, E, D);
  nor nor_1 (Q, clear, and_1_out, nQ);
  nor nor_2 (nQ, Q, and_2_out);
endmodule

// D FF
module MS_D_Flip_flop (
  input  in_1,
  input  D,
  input  Ck,
  output Q,
  output nQ
);

  wire gated_d_latch_1_q, not_1_out;

  Gated_D_Latch gated_d_latch_1 (.D(D), .E(not_1_out), .Q(gated_d_latch_1_q), .clear(1'b0));  // open: nQ
  not not_1 (not_1_out, Ck);
  Gated_D_Latch gated_d_latch_2 (.D(gated_d_latch_1_q), .E(Ck), .Q(Q), .nQ(nQ), .clear(in_1));
endmodule

module _4bit_register (
  input  [3:0] D,
  input  clear,
  input  Ck,
  input  E,
  output [3:0] Q
);

  wire and_1_out;

  and and_1 (and_1_out, Ck, E);
  MS_D_Flip_flop ms_d_flip_flop_1 (.D(D[0]), .Ck(and_1_out), .Q(Q[0]), .in_1(clear));  // open: nQ
  MS_D_Flip_flop ms_d_flip_flop_2 (.D(D[1]), .Ck(and_1_out), .Q(Q[1]), .in_1(clear));  // open: nQ
  MS_D_Flip_flop ms_d_flip_flop_3 (.D(D[2]), .Ck(and_1_out), .Q(Q[2]), .in_1(clear));  // open: nQ
  MS_D_Flip_flop ms_d_flip_flop_4 (.D(D[3]), .Ck(and_1_out), .Q(Q[3]), .in_1(clear));  // open: nQ
endmodule

module _8bit_register (
  input  [7:0] D,
  input  Ck,
  input  E,
  input  clear,
  output [7:0] Q
);

  wire and_1_out;

  and and_1 (and_1_out, Ck, E);
  MS_D_Flip_flop ms_d_flip_flop_1 (.D(D[0]), .Ck(and_1_out), .Q(Q[0]), .in_1(clear));  // open: nQ
  MS_D_Flip_flop ms_d_flip_flop_2 (.D(D[1]), .Ck(and_1_out), .Q(Q[1]), .in_1(clear));  // open: nQ
  MS_D_Flip_flop ms_d_flip_flop_3 (.D(D[2]), .Ck(and_1_out), .Q(Q[2]), .in_1(clear));  // open: nQ
  MS_D_Flip_flop ms_d_flip_flop_4 (.D(D[3]), .Ck(and_1_out), .Q(Q[7]), .in_1(clear));  // open: nQ
  MS_D_Flip_flop ms_d_flip_flop_5 (.D(D[4]), .Ck(and_1_out), .in_1(clear));  // open: Q, nQ
  MS_D_Flip_flop ms_d_flip_flop_6 (.D(D[5]), .Ck(and_1_out), .in_1(clear));  // open: Q, nQ
  MS_D_Flip_flop ms_d_flip_flop_7 (.D(D[6]), .Ck(and_1_out), .in_1(clear));  // open: Q, nQ
  MS_D_Flip_flop ms_d_flip_flop_8 (.D(D[7]), .Ck(and_1_out), .in_1(clear));  // open: Q, nQ

  assign Q[6:3] = {4{Q[7]}};
endmodule
