// Logisim project hw3-mux_LU_shifter.circ as structural Verilog: 6 circuits, main circuit main
module main (
);

  _2x1_mux u_2x1_mux_1 ();  // open: S, I0, I1, O
endmodule

module _2x1_mux (
  input  S,
  input  I0,
  input  I1,
  output O
);

  wire and_1_out, and_2_out, not_1_out;

  not not_1 (not_1_out, S);
  and and_1 (and_1_out, not_1_out, I0);
  and and_2 (and_2_out, S, I1);
  or or_1 (O, and_1_out, and_2_out);
endmodule

module _4x1_mux (
  input  S1,
  input  S0,
  input  I0,
  input  I1,
  input  I2,
  input  I3,
  output out_7
);

  wire and_1_out, and_2_out, and_3_out, and_4_out, not_1_out, not_2_out;

  not not_1 (not_1_out, S1);
  not not_2 (not_2_out, S0);
  and and_1 (and_1_out, not_2_out, not_1_out, I0);
  and and_2 (and_2_out, S0, not_1_out, I1);
  and and_3 (and_3_out, not_2_out, S1, I2);
  and and_4 (and_4_out, S0, S1, I3);
  or or_1 (out_7, and_1_out, and_2_out, and_3_out, and_4_out);
endmodule

// 1 LU
module _1bit_LU (
  input  A,
  input  B,
  input  S1,
  input  S0,
  output out_5
);

  wire and_1_out, not_1_out, or_1_out, xor_1_out;

  and and_1 (and_1_out, A, B);
  or or_1 (or_1_out, A, B);
  xor xor_1 (xor_1_out, A, B);
  not not_1 (not_1_out, A);
  _4x1_mux u_4x1_mux_1 (.S1(S1), .S0(S0), .I0(and_1_out), .I1(or_1_out), .I2(xor_1_out), .I3(not_1_out), .out_7(out_5));
endmodule

module _4bit_LU (
  input  [3:0] A,
  input  [3:0] B,
  input  S1,
  input  S0,
  output [3:0] F
);

  _1bit_LU u_1bit_lu_1 (.A(A[0]), .B(B[0]), .S1(S1), .S0(S0), .out_5(F[0]));
  _1bit_LU u_1bit_lu_2 (.A(A[1]), .B(B[1]), .S1(S1), .S0(S0), .out_5(F[1]));
  _1bit_LU u_1bit_lu_3 (.A(A[2]), .B(B[2]), .S1(S1), .S0(S0), .out_5(F[2]));
  _1bit_LU u_1bit_lu_4 (.A(A[3]), .B(B[3]), .S1(S1), .S0(S0), .out_5(F[3]));
endmodule

module _4bit_shifter (
  input  [3:0] in_1,
  input  S1,
  input  S0,
  output [3:0] out_4
);

  _4x1_mux u_4x1_mux_1 (.S1(S1), .S0(S0), .I0(in_1[0]), .I1(in_1[1]), .I2(1'b0), .I3(1'b0), .out_7(out_4[0]));
  _4x1_mux u_4x1_mux_2 (.S1(S1), .S0(S0), .I0(in_1[1]), .I1(in_1[2]), .I2(in_1[0]), .out_7(out_4[1]));  // open: I3
  _4x1_mux u_4x1_mux_3 (.S1(S1), .S0(S0), .I0(in_1[2]), .I1(in_1[3]), .I2(in_1[1]), .out_7(out_4[2]));  // open: I3
  _4x1_mux u_4x1_mux_4 (.S1(S1), .S0(S0), .I0(in_1[3]), .I1(1'b0), .I2(in_1[2]), .out_7(out_4[3]));  // open: I3
endmodule
